// Logisim project 4x4Adder.circ as structural Verilog: 1 circuit, main circuit main
module main (
  input  B0,
  input  A3,
  input  A2,
  input  A1,
  input  A0,
  input  B1,
  input  B2,
  input  B3
);

  wire A0B0_out, A0B1_out, A0B2_out, A0B3_2_out, A0B3_3_out, A0B3_4_out, A0B3_out, A1B0_out, A1B1_out,
       A1B2_out, A2B0_out, A2B1_out, A2B2_out, A3B0_out, A3B1_out, A3B2_out, adder_1_cout, adder_1_out,
       adder_2_cout, adder_2_out, adder_3_cout, adder_3_out, adder_4_cout, adder_4_out, adder_5_cout,
       adder_5_out, adder_6_cout, adder_6_out, adder_7_cout, adder_7_out, adder_8_cout, adder_8_out,
       adder_9_cout, adder_9_out, adder_10_cout, adder_10_out, adder_11_cout, adder_11_out, adder_12_cout,
       adder_12_out;

  and A0B3 (A0B3_out, A3, B3);
  and A0B3_2 (A0B3_2_out, A2, B3);
  Adder #(.width(1)) adder_1 (
    .a(adder_3_cout), .b(A0B3_out), .out(adder_1_out), .cin(adder_2_cout), .cout(adder_1_cout));
  and A3B2 (A3B2_out, A3, B2);
  Adder #(.width(1)) adder_2 (
    .a(adder_3_out), .b(A0B3_2_out), .out(adder_2_out), .cin(adder_6_cout), .cout(adder_2_cout));
  and A3B1 (A3B1_out, A3, B1);
  and A2B2 (A2B2_out, A2, B2);
  Adder #(.width(1)) adder_3 (
    .a(adder_4_cout), .b(A3B2_out), .out(adder_3_out), .cin(adder_5_cout), .cout(adder_3_cout));
  and A0B3_3 (A0B3_3_out, A1, B3);
  // Probe on adder_1_cout
  // Probe on adder_1_out
  and A2B1 (A2B1_out, A2, B1);
  Adder #(.width(1)) adder_4 (.a(adder_7_cout), .b(A3B1_out), .out(adder_4_out), .cin(1'b0), .cout(adder_4_cout));
  and A1B2 (A1B2_out, A1, B2);
  Adder #(.width(1)) adder_5 (
    .a(adder_4_out), .b(A2B2_out), .out(adder_5_out), .cin(adder_8_cout), .cout(adder_5_cout));
  and A0B3_4 (A0B3_4_out, A0, B3);
  Adder #(.width(1)) adder_6 (
    .a(adder_5_out), .b(A0B3_3_out), .out(adder_6_out), .cin(adder_9_cout), .cout(adder_6_cout));
  // Probe on adder_6_out
  // Probe on adder_2_out
  and A3B0 (A3B0_out, A3, B0);
  Adder #(.width(1)) adder_7 (.a(A3B0_out), .b(A2B1_out), .out(adder_7_out), .cin(adder_11_cout), .cout(adder_7_cout));
  and A0B2 (A0B2_out, A0, B2);
  Adder #(.width(1)) adder_8 (
    .a(adder_7_out), .b(A1B2_out), .out(adder_8_out), .cin(adder_10_cout), .cout(adder_8_cout));
  Adder #(.width(1)) adder_9 (.a(adder_8_out), .b(A0B3_4_out), .out(adder_9_out), .cin(1'b0), .cout(adder_9_cout));
  // Probe on adder_12_out
  // Probe on adder_10_out
  // Probe on adder_9_out
  and A2B0 (A2B0_out, A2, B0);
  and A1B1 (A1B1_out, A1, B1);
  Adder #(.width(1)) adder_10 (.a(adder_11_out), .b(A0B2_out), .out(adder_10_out), .cin(1'b0), .cout(adder_10_cout));
  // Probe on A0B0_out
  and A1B0 (A1B0_out, A1, B0);
  and A0B1 (A0B1_out, A0, B1);
  Adder #(.width(1)) adder_11 (
    .a(A2B0_out), .b(A1B1_out), .out(adder_11_out), .cin(adder_12_cout), .cout(adder_11_cout));
  and A0B0 (A0B0_out, A0, B0);
  Adder #(.width(1)) adder_12 (.a(A1B0_out), .b(A0B1_out), .out(adder_12_out), .cin(1'b0), .cout(adder_12_cout));
endmodule
