// Logisim project Lab6.circ as structural Verilog: 1 circuit, main circuit main
module main (
  input  B2,
  input  B1,
  input  A2,
  input  A1,
  input  M,
  input  B1_2,
  input  B0,
  input  A1_2,
  input  A0,
  input  [2:0] A,
  input  [2:0] B
);

  wire adder_2_cout, adder_2_out, adder_3_cout, adder_3_out, and_1_out, and_2_out, and_3_out, and_4_out,
       and_5_out, and_6_out, and_7_out, comparator_1_eq, comparator_1_gt, comparator_1_lt, not_1_out,
       not_2_out, not_4_out, or_1_out, or_2_out, xnor_1_out, xnor_2_out, xor_1_out, xor_2_out;
  wire [2:0] adder_1_out, multiplier_1_out, subtractor_1_out;

  and and_1 (and_1_out, B2, B1, not_4_out);
  and and_2 (and_2_out, B2, not_2_out);
  and and_3 (and_3_out, B1, not_2_out, not_4_out);
  or or_1 (or_1_out, and_1_out, and_3_out, and_2_out);
  xnor xnor_1 (xnor_1_out, B2, A2);
  // Probe on or_1_out
  xnor xnor_2 (xnor_2_out, B1, A1);
  and and_4 (and_4_out, xnor_1_out, xnor_2_out);
  // Probe on or_2_out
  // Probe on and_4_out
  Adder #(.width(3)) adder_1 (.a(B), .b(A), .out(adder_1_out), .cin(1'b0));  // open: cout
  and and_5 (and_5_out, not_1_out, not_1_out, A2);
  and and_6 (and_6_out, not_1_out, A2, A1);
  or or_2 (or_2_out, and_6_out, and_5_out, and_7_out);
  Multiplier #(.width(3)) multiplier_1 (.a(B), .b(A), .out(multiplier_1_out), .cin(3'b000));  // open: cout
  not not_1 (not_1_out, B2);
  and and_7 (and_7_out, not_1_out, A1);
  // Probe on subtractor_1_out
  Subtractor #(.width(3)) subtractor_1 (.a(multiplier_1_out), .b(B), .out(subtractor_1_out), .bin(1'b0));  // open: bout
  // Probe on adder_1_out
  not not_2 (not_2_out, A2);
  not not_3 (not_1_out, B1);
  Comparator #(.width(3)) comparator_1 (
    .a(subtractor_1_out), .b(adder_1_out), .gt(comparator_1_gt), .eq(comparator_1_eq), .lt(comparator_1_lt));
  not not_4 (not_4_out, A1);
  // Probe on comparator_1_gt
  // Probe on comparator_1_eq
  // Probe on comparator_1_lt
  xor xor_1 (xor_1_out, M, B0);
  xor xor_2 (xor_2_out, M, B1_2);
  Adder #(.width(1)) adder_2 (.a(A0), .b(xor_1_out), .out(adder_2_out), .cin(M), .cout(adder_2_cout));
  Adder #(.width(1)) adder_3 (.a(A1_2), .b(xor_2_out), .out(adder_3_out), .cin(adder_2_cout), .cout(adder_3_cout));
  // Probe on adder_3_cout
  // Probe on adder_3_out
  // Probe on adder_2_out
endmodule
