// Logisim project DLD_Lab9.circ as structural Verilog: 1 circuit, main circuit main
module main (
  input  S,
  input  EN,
  input  [15:0] I0___I16,
  input  [2:0] S2_S1_S0,
  input  R,
  input  S3,
  input  D,
  input  EN_2,
  input  [2:0] in_9,
  input  WE,
  input  [1:0] A,
  input  [1:0] B,
  input  WE_2,
  input  [1:0] in_14,
  input  [1:0] in_15,
  output Q,
  output Y,
  output Q_prime,
  output Q_2,
  output Y0,
  output Q_prime_2,
  output Y1,
  output Y2,
  output Y3,
  output Y4,
  output Y5,
  output Y6,
  output Y7,
  output out_29,
  output out_30,
  output out_31,
  output out_32,
  output out_33,
  output out_34
);

  wire adder_1_cout, and_1_out, and_2_out, and_3_out, and_4_out, and_5_out, and_6_out, and_7_out, and_8_out,
       and_9_out, and_10_out, and_11_out, and_12_out, multiplexer_1_out, multiplexer_2_out, nand_1_out,
       nand_2_out, nand_3_out, nand_4_out, nand_5_out, nor_2_out, nor_4_out, nor_6_out, nor_8_out,
       nor_10_out, nor_12_out, not_1_out, not_2_out, not_3_out, not_4_out, not_5_out, not_6_out;
  wire [1:0] adder_1_out, multiplier_1_cout, multiplier_1_out;

  Demultiplexer #(.select(3), .enable("false")) demultiplexer_1 (
    .out0(Y0), .out1(Y1), .out2(Y2), .out3(Y3), .out4(Y4), .out5(Y5), .out6(Y6), .out7(Y7), .in(1'b1),
    .sel(in_9));
  Multiplier #(.width(2)) multiplier_1 (
    .a(in_14), .b(in_15), .out(multiplier_1_out), .cin(2'b00), .cout(multiplier_1_cout));
  Multiplexer #(.select(3), .enable("false")) multiplexer_1 (
    .in0(I0___I16[0]), .in1(I0___I16[1]), .in2(I0___I16[2]), .in3(I0___I16[3]), .in4(I0___I16[4]),
    .in5(I0___I16[5]), .in6(I0___I16[6]), .in7(I0___I16[7]), .out(multiplexer_1_out), .sel(S2_S1_S0));
  Multiplexer #(.select(3), .enable("false")) multiplexer_2 (
    .in0(I0___I16[8]), .in1(I0___I16[9]), .in2(I0___I16[10]), .in3(I0___I16[11]), .in4(I0___I16[12]),
    .in5(I0___I16[13]), .in6(I0___I16[14]), .in7(I0___I16[15]), .out(multiplexer_2_out), .sel(S2_S1_S0));
  and and_1 (and_1_out, WE_2, not_1_out);
  not not_1 (not_1_out, multiplier_1_cout[0]);
  and and_2 (and_2_out, WE_2, multiplier_1_cout[0]);
  and and_3 (and_3_out, WE_2, not_2_out);
  not not_2 (not_2_out, multiplier_1_out[1]);
  and and_4 (and_4_out, WE_2, multiplier_1_out[1]);
  and and_5 (and_5_out, WE_2, not_3_out);
  not not_3 (not_3_out, multiplier_1_out[0]);
  and and_6 (and_6_out, WE_2, multiplier_1_out[0]);
  Multiplexer #(.enable("false")) multiplexer_3 (.in0(multiplexer_1_out), .in1(multiplexer_2_out), .out(Y), .sel(S3));
  nor nor_1 (out_33, and_1_out, nor_2_out);
  nor nor_2 (nor_2_out, out_33, and_2_out);
  nor nor_3 (out_32, and_3_out, nor_4_out);
  nor nor_4 (nor_4_out, out_32, and_4_out);
  nor nor_5 (out_34, and_5_out, nor_6_out);
  nor nor_6 (nor_6_out, out_34, and_6_out);
  nand nand_1 (nand_1_out, S, EN);
  nand nand_2 (nand_2_out, EN, R);
  nand nand_3 (nand_3_out, D, EN_2);
  nand nand_4 (nand_4_out, D, D);
  nand nand_5 (nand_5_out, nand_4_out, EN_2);
  Adder #(.width(2)) adder_1 (.a(A), .b(B), .out(adder_1_out), .cin(1'b0), .cout(adder_1_cout));
  nand nand_6 (Q, nand_1_out, Q_prime);
  nand nand_7 (Q_prime, Q, nand_2_out);
  nand nand_8 (Q_2, nand_3_out, Q_prime_2);
  nand nand_9 (Q_prime_2, Q_2, nand_5_out);
  not not_4 (not_4_out, adder_1_out[1]);
  not not_5 (not_5_out, adder_1_out[1]);
  not not_6 (not_6_out, adder_1_cout);
  and and_7 (and_7_out, WE, not_4_out);
  and and_8 (and_8_out, WE, adder_1_out[0]);
  and and_9 (and_9_out, WE, not_5_out);
  and and_10 (and_10_out, WE, adder_1_out[1]);
  and and_11 (and_11_out, WE, not_6_out);
  and and_12 (and_12_out, WE, adder_1_cout);
  nor nor_7 (out_30, and_7_out, nor_8_out);
  nor nor_8 (nor_8_out, out_30, and_8_out);
  nor nor_9 (out_29, and_9_out, nor_10_out);
  nor nor_10 (nor_10_out, out_29, and_10_out);
  nor nor_11 (out_31, and_11_out, nor_12_out);
  nor nor_12 (nor_12_out, out_31, and_12_out);
endmodule
